// Logisim project Diferença.circ as structural Verilog: 10 circuits, main circuit main
module main (
  input  Alet_4,
  input  Alet_3,
  input  Alet_2,
  input  Alet_1,
  input  Bit_4,
  input  Bit3,
  input  Bit2,
  input  Bit1,
  output Led4,
  output Led3,
  output Led2,
  output Led1
);

  wire a_b_1_dif_1, a_b_1_dif_2, a_b_1_dif_3, a_b_1_dif_4, b_a_1_dif_1, b_a_1_dif_2, b_a_1_dif_3,
       b_a_1_dif_4, portas_and_para_multiplex_1_out_9, portas_and_para_multiplex_1_out_10,
       portas_and_para_multiplex_1_out_11, portas_and_para_multiplex_1_out_12,
       portas_and_para_multiplex_2_out_9, portas_and_para_multiplex_2_out_10,
       portas_and_para_multiplex_2_out_11, portas_and_para_multiplex_2_out_12,
       portas_and_para_multiplex_3_out_9, portas_and_para_multiplex_3_out_10,
       portas_and_para_multiplex_3_out_11, portas_and_para_multiplex_3_out_12,
       portas_and_para_multiplex_4_out_9, portas_and_para_multiplex_4_out_10,
       portas_and_para_multiplex_4_out_11, portas_and_para_multiplex_4_out_12, saida_a_b, saida_b_a;

  Multiplex multiplex_1 (
    .A3(Alet_4), .A2(Alet_3), .A1(Alet_2), .A0(Alet_1), .B3(Bit_4), .B2(Bit3), .B1(Bit2), .B0(Bit1),
    .A_B(saida_a_b), .B_A(saida_b_a));  // open: out_10
  portas_and_para_multiplex portas_and_para_multiplex_1 (
    .in_1(Bit_4), .in_2(Bit3), .in_3(Bit2), .in_4(Bit1), .in_5(saida_b_a), .in_6(saida_b_a),
    .in_7(saida_b_a), .in_8(saida_b_a), .out_9(portas_and_para_multiplex_1_out_9),
    .out_10(portas_and_para_multiplex_1_out_10), .out_11(portas_and_para_multiplex_1_out_11),
    .out_12(portas_and_para_multiplex_1_out_12));
  portas_and_para_multiplex portas_and_para_multiplex_2 (
    .in_1(Alet_4), .in_2(Alet_3), .in_3(Alet_2), .in_4(Alet_1), .in_5(saida_a_b), .in_6(saida_a_b),
    .in_7(saida_a_b), .in_8(saida_a_b), .out_9(portas_and_para_multiplex_2_out_9),
    .out_10(portas_and_para_multiplex_2_out_10), .out_11(portas_and_para_multiplex_2_out_11),
    .out_12(portas_and_para_multiplex_2_out_12));
  portas_and_para_multiplex portas_and_para_multiplex_3 (
    .in_1(Bit_4), .in_2(Bit3), .in_3(Bit2), .in_4(Bit1), .in_5(saida_a_b), .in_6(saida_a_b),
    .in_7(saida_a_b), .in_8(saida_a_b), .out_9(portas_and_para_multiplex_3_out_9),
    .out_10(portas_and_para_multiplex_3_out_10), .out_11(portas_and_para_multiplex_3_out_11),
    .out_12(portas_and_para_multiplex_3_out_12));
  portas_and_para_multiplex portas_and_para_multiplex_4 (
    .in_1(Alet_4), .in_2(Alet_3), .in_3(Alet_2), .in_4(Alet_1), .in_5(saida_b_a), .in_6(saida_b_a),
    .in_7(saida_b_a), .in_8(saida_b_a), .out_9(portas_and_para_multiplex_4_out_9),
    .out_10(portas_and_para_multiplex_4_out_10), .out_11(portas_and_para_multiplex_4_out_11),
    .out_12(portas_and_para_multiplex_4_out_12));
  A_B a_b_1 (
    .Alet_4(portas_and_para_multiplex_2_out_9), .Alet_3(portas_and_para_multiplex_2_out_10),
    .Alet_2(portas_and_para_multiplex_2_out_11), .Alet_1(portas_and_para_multiplex_2_out_12),
    .Bit_4(portas_and_para_multiplex_3_out_9), .Bit3(portas_and_para_multiplex_3_out_10),
    .Bit2(portas_and_para_multiplex_3_out_11), .Bit1(portas_and_para_multiplex_3_out_12),
    .Dif_4(a_b_1_dif_4), .Dif_3(a_b_1_dif_3), .Dif_2(a_b_1_dif_2), .Dif_1(a_b_1_dif_1));  // open: Dif_5
  B_A b_a_1 (
    .Bit_4(portas_and_para_multiplex_1_out_9), .Bit3(portas_and_para_multiplex_1_out_10),
    .Bit2(portas_and_para_multiplex_1_out_11), .Bit1(portas_and_para_multiplex_1_out_12),
    .Alet_4(portas_and_para_multiplex_4_out_9), .Alet_3(portas_and_para_multiplex_4_out_10),
    .Alet_2(portas_and_para_multiplex_4_out_11), .Alet_1(portas_and_para_multiplex_4_out_12),
    .Dif_4(b_a_1_dif_4), .Dif_3(b_a_1_dif_3), .Dif_2(b_a_1_dif_2), .Dif_1(b_a_1_dif_1));  // open: Dif_5
  portas_or_para_multiplex portas_or_para_multiplex_1 (
    .in_1(a_b_1_dif_4), .in_2(a_b_1_dif_3), .in_3(a_b_1_dif_2), .in_4(a_b_1_dif_1), .in_5(b_a_1_dif_4),
    .in_6(b_a_1_dif_3), .in_7(b_a_1_dif_2), .in_8(b_a_1_dif_1), .out_9(Led4), .out_10(Led3), .out_11(Led2),
    .out_12(Led1));
endmodule

module Somador1bit (
  input  Cin,
  input  B,
  input  A,
  output S,
  output Cout
);

  wire and_1_out, and_2_out, and_3_out, xor_1_out;

  xor xor_1 (xor_1_out, A, B);
  and and_1 (and_1_out, B, A);
  and and_2 (and_2_out, A, Cin);
  and and_3 (and_3_out, Cin, B);
  or or_1 (Cout, and_1_out, and_2_out, and_3_out);
  xor xor_2 (S, xor_1_out, Cin);
endmodule

module Somador4bits (
  input  A4,
  input  A3,
  input  A2,
  input  A1,
  input  I4,
  input  I3,
  input  I2,
  input  I1,
  output Sf5,
  output Sf4,
  output Sf3,
  output Sf2,
  output Sf1
);

  wire somador1bit_2_cout, somador1bit_3_cout, somador1bit_4_cout;

  Somador1bit somador1bit_1 (.Cin(somador1bit_2_cout), .B(I4), .A(A4), .S(Sf4), .Cout(Sf5));
  Somador1bit somador1bit_2 (.Cin(somador1bit_3_cout), .B(I3), .A(A3), .S(Sf3), .Cout(somador1bit_2_cout));
  Somador1bit somador1bit_3 (.Cin(somador1bit_4_cout), .B(I2), .A(A2), .S(Sf2), .Cout(somador1bit_3_cout));
  Somador1bit somador1bit_4 (.Cin(1'b0), .B(I1), .A(A1), .S(Sf1), .Cout(somador1bit_4_cout));
endmodule

module Complementode2 (
  input  Iu1,
  input  Iu2,
  input  Iu3,
  input  Iu4,
  output Ou1,
  output Ou2,
  output Ou3,
  output Ou4
);

  wire not_1_out, not_2_out, not_3_out, not_4_out, somador1bit_1_cout, somador1bit_2_cout, somador1bit_4_cout;

  not not_1 (not_1_out, Iu1);
  not not_2 (not_2_out, Iu2);
  not not_3 (not_3_out, Iu3);
  not not_4 (not_4_out, Iu4);
  Somador1bit somador1bit_1 (.Cin(1'b0), .B(not_1_out), .A(1'b1), .S(Ou1), .Cout(somador1bit_1_cout));
  Somador1bit somador1bit_2 (.Cin(somador1bit_1_cout), .B(not_2_out), .A(1'b0), .S(Ou2), .Cout(somador1bit_2_cout));
  Somador1bit somador1bit_3 (.Cin(somador1bit_4_cout), .B(not_4_out), .A(1'b0), .S(Ou4));  // open: Cout
  Somador1bit somador1bit_4 (.Cin(somador1bit_2_cout), .B(not_3_out), .A(1'b0), .S(Ou3), .Cout(somador1bit_4_cout));
endmodule

module Maior_ou_menor (
  input  Alet_4,
  input  Alet_3,
  input  Alet_2,
  input  Alet_1,
  input  Bit_4,
  input  Bit3,
  input  Bit2,
  input  Bit1,
  output [3:0] out_9
);

  wire a_b_1_dif_5, not_1_out;
  wire [3:0] a_b_1_dif_1, b_a_1_dif_1;

  A_B a_b_1 (
    .Alet_4(Alet_4), .Alet_3(Alet_3), .Alet_2(Alet_2), .Alet_1(Alet_1), .Bit_4(Bit_4), .Bit3(Bit3),
    .Bit2(Bit2), .Bit1(Bit1), .Dif_5(a_b_1_dif_5), .Dif_4(a_b_1_dif_1[3]), .Dif_3(a_b_1_dif_1[2]),
    .Dif_2(a_b_1_dif_1[1]), .Dif_1(a_b_1_dif_1[0]));
  B_A b_a_1 (
    .Bit_4(Bit_4), .Bit3(Bit3), .Bit2(Bit2), .Bit1(Bit1), .Alet_4(Alet_4), .Alet_3(Alet_3), .Alet_2(Alet_2),
    .Alet_1(Alet_1), .Dif_4(b_a_1_dif_1[3]), .Dif_3(b_a_1_dif_1[2]), .Dif_2(b_a_1_dif_1[1]),
    .Dif_1(b_a_1_dif_1[0]));  // open: Dif_5
  Multiplexer #(.width(4), .enable("false")) multiplexer_1 (
    .in0(a_b_1_dif_1), .in1(b_a_1_dif_1), .out(out_9), .sel(not_1_out));
  not not_1 (not_1_out, a_b_1_dif_5);
endmodule

module A_B (
  input  Alet_4,
  input  Alet_3,
  input  Alet_2,
  input  Alet_1,
  input  Bit_4,
  input  Bit3,
  input  Bit2,
  input  Bit1,
  output Dif_5,
  output Dif_4,
  output Dif_3,
  output Dif_2,
  output Dif_1
);

  wire complementode2_1_ou1, complementode2_1_ou2, complementode2_1_ou3, complementode2_1_ou4,
       somador4bits_1_sf5;

  Complementode2 complementode2_1 (
    .Iu1(Bit1), .Iu2(Bit2), .Iu3(Bit3), .Iu4(Bit_4), .Ou1(complementode2_1_ou1), .Ou2(complementode2_1_ou2),
    .Ou3(complementode2_1_ou3), .Ou4(complementode2_1_ou4));
  Somador4bits somador4bits_1 (
    .A4(Alet_4), .A3(Alet_3), .A2(Alet_2), .A1(Alet_1), .I4(complementode2_1_ou4), .I3(complementode2_1_ou3),
    .I2(complementode2_1_ou2), .I1(complementode2_1_ou1), .Sf5(somador4bits_1_sf5), .Sf4(Dif_4), .Sf3(Dif_3),
    .Sf2(Dif_2), .Sf1(Dif_1));

  assign Dif_5 = Dif_4;
endmodule

module B_A (
  input  Alet_4,
  input  Alet_3,
  input  Alet_2,
  input  Alet_1,
  input  Bit_4,
  input  Bit3,
  input  Bit2,
  input  Bit1,
  output Dif_5,
  output Dif_4,
  output Dif_3,
  output Dif_2,
  output Dif_1
);

  wire complementode2_1_ou1, complementode2_1_ou2, complementode2_1_ou3, complementode2_1_ou4,
       somador4bits_1_sf5;

  Complementode2 complementode2_1 (
    .Iu1(Alet_1), .Iu2(Alet_2), .Iu3(Alet_3), .Iu4(Alet_4), .Ou1(complementode2_1_ou1),
    .Ou2(complementode2_1_ou2), .Ou3(complementode2_1_ou3), .Ou4(complementode2_1_ou4));
  Somador4bits somador4bits_1 (
    .A4(complementode2_1_ou4), .A3(complementode2_1_ou3), .A2(complementode2_1_ou2),
    .A1(complementode2_1_ou1), .I4(Bit_4), .I3(Bit3), .I2(Bit2), .I1(Bit1), .Sf5(somador4bits_1_sf5),
    .Sf4(Dif_4), .Sf3(Dif_3), .Sf2(Dif_2), .Sf1(Dif_1));

  assign Dif_5 = Dif_4;
endmodule

module Multiplex (
  input  A3,
  input  A2,
  input  A1,
  input  A0,
  input  B3,
  input  B2,
  input  B1,
  input  B0,
  output A_B,
  output out_10,
  output B_A
);

  wire and_2_out, and_3_out, and_4_out, and_5_out, and_6_out, and_7_out, and_8_out, and_9_out, not_1_out,
       not_2_out, not_3_out, not_4_out, not_5_out, not_6_out, not_7_out, not_8_out, not_9_out, not_10_out,
       not_11_out, not_12_out, xor_1_out, xor_2_out, xor_3_out, xor_4_out;

  and and_1 (out_10, not_1_out, not_2_out, not_3_out, not_4_out);
  xor xor_1 (xor_1_out, A3, B3);
  not not_1 (not_1_out, xor_1_out);
  xor xor_2 (xor_2_out, A2, B2);
  not not_2 (not_2_out, xor_2_out);
  xor xor_3 (xor_3_out, A1, B1);
  not not_3 (not_3_out, xor_3_out);
  xor xor_4 (xor_4_out, A0, B0);
  not not_4 (not_4_out, xor_4_out);
  not not_5 (not_5_out, B3);
  and and_2 (and_2_out, not_5_out, A3);
  not not_6 (not_6_out, B2);
  and and_3 (and_3_out, not_6_out, not_1_out, A2);
  and and_4 (and_4_out, A1, not_1_out, not_2_out, not_7_out);
  not not_7 (not_7_out, B1);
  and and_5 (and_5_out, A0, not_1_out, not_2_out, not_3_out, not_8_out);
  not not_8 (not_8_out, B0);
  or or_1 (A_B, and_2_out, and_3_out, and_4_out, and_5_out);
  not not_9 (not_9_out, A3);
  not not_10 (not_10_out, A2);
  not not_11 (not_11_out, A1);
  not not_12 (not_12_out, A0);
  and and_6 (and_6_out, not_9_out, B3);
  and and_7 (and_7_out, not_10_out, not_1_out, B2);
  and and_8 (and_8_out, not_11_out, not_1_out, not_2_out, B1);
  and and_9 (and_9_out, not_12_out, not_1_out, not_2_out, not_3_out, B0);
  or or_2 (B_A, and_6_out, and_7_out, and_8_out, and_9_out);
endmodule

module portas_and_para_multiplex (
  input  in_1,
  input  in_2,
  input  in_3,
  input  in_4,
  input  in_5,
  input  in_6,
  input  in_7,
  input  in_8,
  output out_9,
  output out_10,
  output out_11,
  output out_12
);

  and and_1 (out_9, in_1, in_5);
  and and_2 (out_10, in_2, in_6);
  and and_3 (out_11, in_3, in_7);
  and and_4 (out_12, in_4, in_8);
endmodule

module portas_or_para_multiplex (
  input  in_1,
  input  in_2,
  input  in_3,
  input  in_4,
  input  in_5,
  input  in_6,
  input  in_7,
  input  in_8,
  output out_9,
  output out_10,
  output out_11,
  output out_12
);

  or or_1 (out_9, in_1, in_5);
  or or_2 (out_10, in_2, in_6);
  or or_3 (out_11, in_3, in_7);
  or or_4 (out_12, in_4, in_8);
endmodule
