// Logisim project LedRGB.circ as structural Verilog: 3 circuits, main circuit main
module main (
  input  in_1,
  input  in_2,
  input  in_3,
  input  in_4
);

  wire [7:0] and_1_out, divisor_1_out_azul, divisor_1_out_vermelhoo;

  Divisor divisor_1 (
    .plus_esquerdav(in_1), .in_2(in_2), .in_3(in_3), .plus_direitav(in_4), .plus_esquerdaa(in_1),
    .in_6(in_2), .in_7(in_3), .plus_direitaa(in_4), .OUT_Vermelhoo(divisor_1_out_vermelhoo),
    .OUT_Azul(divisor_1_out_azul));
  assign and_1_out = {8{1'b1}} & divisor_1_out_vermelhoo;  // AND_Gate and_1, 8 bits wide
  // RGBLed #(.multibit("true")) LED_VERDE: pin names not known; wires that end beside it: and_1_out
  // RGBLed #(.multibit("true")) LED: pin names not known; wires that end beside it: divisor_1_out_azul, divisor_1_out_vermelhoo

  // Notes on the sheet:
  //   and_1 drives only 1 and floats otherwise
endmodule

module Divisor (
  input  plus_esquerdav,
  input  in_2,
  input  in_3,
  input  plus_direitav,
  input  plus_esquerdaa,
  input  in_6,
  input  in_7,
  input  plus_direitaa,
  output [7:0] OUT_Vermelhoo,
  output [7:0] OUT_Azul
);

  not not_1 (OUT_Vermelhoo[6], in_2);
  not not_2 (OUT_Vermelhoo[7], plus_esquerdav);
  not not_3 (OUT_Vermelhoo[4], plus_direitav);
  not not_4 (OUT_Vermelhoo[5], in_3);

  assign OUT_Azul = {plus_esquerdaa, in_6, in_7, plus_direitaa, 4'b1111};
  assign OUT_Vermelhoo[3:0] = 4'b1111;
endmodule

module LED_RGB (
  input  in_1,
  input  in_2,
  input  in_3,
  input  in_4
);

  wire [7:0] and_1_out, divisor_1_out_azul, divisor_1_out_vermelhoo;

  Divisor divisor_1 (
    .plus_esquerdav(in_1), .in_2(in_2), .in_3(in_3), .plus_direitav(in_4), .plus_esquerdaa(in_1),
    .in_6(in_2), .in_7(in_3), .plus_direitaa(in_4), .OUT_Vermelhoo(divisor_1_out_vermelhoo),
    .OUT_Azul(divisor_1_out_azul));
  assign and_1_out = {8{1'b1}} & divisor_1_out_vermelhoo;  // AND_Gate and_1, 8 bits wide
  // RGBLed #(.multibit("true")) LED_VERDE: pin names not known; wires that end beside it: and_1_out
  // RGBLed #(.multibit("true")) LED: pin names not known; wires that end beside it: divisor_1_out_azul, divisor_1_out_vermelhoo

  // Notes on the sheet:
  //   and_1 drives only 1 and floats otherwise
endmodule
