// Logisim project Principal _Projeto_completo.circ as structural Verilog: 1 circuit, main circuit main
// Display
module main (
  input  in_1,
  input  in_2,
  input  in_3,
  input  in_4,
  input  in_5,
  input  in_6,
  input  in_7,
  input  in_8
);

  wire Comparador_out_9, Display_p5, Display_p6, Display_p7, Display_p8, Display_p9, Display_p10,
       Display_p11, LED_RGB_p9, LED_RGB_p10;
  wire [3:0] \Circuito_completo_diferença_out_10 ;

  \Diferença_main  \Circuito_completo_diferença  (
    .Alet_4(in_1), .Alet_3(in_2), .Alet_2(in_3), .Alet_1(in_4), .\Bit_de_seleção (Comparador_out_9),
    .Bit_4(in_5), .Bit3(in_6), .Bit2(in_7), .Bit1(in_8), .out_10(\Circuito_completo_diferença_out_10 ));
  LED led_1 (.in(Comparador_out_9));
  comparador Comparador (
    .in_1(in_1), .C8(in_5), .in_3(in_2), .C4(in_6), .in_5(in_3), .C2(in_7), .in_7(in_4), .C1(in_8),
    .out_9(Comparador_out_9));
  // Divisor LED_RGB: pin names not known; wires that end beside it: \Circuito_completo_diferença_out_10 [3], \Circuito_completo_diferença_out_10 [2], \Circuito_completo_diferença_out_10 [1], \Circuito_completo_diferença_out_10 [0], \Circuito_completo_diferença_out_10 [1], \Circuito_completo_diferença_out_10 [0], \Circuito_completo_diferença_out_10 [1], \Circuito_completo_diferença_out_10 [0], LED_RGB_p9, LED_RGB_p10
  // circuito Display: pin names not known; wires that end beside it: in_5, in_6, in_7, in_8, Display_p5, Display_p6, Display_p7, Display_p8, Display_p9, Display_p10, Display_p11
  // RGBLed #(.multibit("true")) LED_2: pin names not known; wires that end beside it: \Circuito_completo_diferença_out_10 [3], \Circuito_completo_diferença_out_10 [2], \Circuito_completo_diferença_out_10 [1], \Circuito_completo_diferença_out_10 [0], LED_RGB_p9, LED_RGB_p10
  _7_Segment_Display u_7_segment_display_1 (
    .g(Display_p11), .f(Display_p10), .a(Display_p5), .b(Display_p6), .e(Display_p9), .d(Display_p8),
    .c(Display_p7));  // open: dp
endmodule
