// Logisim project Principal_Projeto_completo_finalizado.circ as structural Verilog: 4 circuits, main circuit main
module main (
  input  in_1,
  input  Palpite,
  input  [3:0] in_3,
  output [7:0] Vermelho,
  output [7:0] Azul,
  output out_6
);

  wire Comparador_out_9, decoder_1_a, decoder_1_b, decoder_1_c, decoder_1_d, decoder_1_e, decoder_1_f,
       decoder_1_g, main_1_led1, main_1_led2, main_1_led3, main_1_led4;
  wire [3:0] random_1_out;
  wire [7:0] divisor_1_p9, divisor_1_p10;

  Random #(.width(4), .trigger("falling")) random_1 (.clk(in_1), .out(random_1_out));  // open: next, clr
  \Diferença_main  main_1 (
    .Alet_4(random_1_out[3]), .Alet_3(random_1_out[2]), .Alet_2(random_1_out[1]), .Alet_1(random_1_out[0]),
    .Bit_4(in_3[3]), .Bit3(in_3[2]), .Bit2(in_3[1]), .Bit1(in_3[0]), .Led4(main_1_led4), .Led3(main_1_led3),
    .Led2(main_1_led2), .Led1(main_1_led1));
  comparador Comparador (
    .in_1(random_1_out[3]), .C8(in_3[3]), .in_3(random_1_out[2]), .C4(in_3[2]), .in_5(random_1_out[1]),
    .C2(in_3[1]), .in_7(random_1_out[0]), .C1(in_3[0]), .out_9(Comparador_out_9));
  // Divisor divisor_1: pin names not known; wires that end beside it: main_1_led4, main_1_led3, main_1_led2, main_1_led1, main_1_led4, main_1_led3, main_1_led2, main_1_led1, divisor_1_p9, divisor_1_p10
  LED led_1 (.in(out_6));
  and and_1 (out_6, Comparador_out_9, Palpite);
  decoder decoder_1 (
    .P0(in_3[3]), .P1(in_3[2]), .P2(in_3[1]), .P3(in_3[0]), .A(decoder_1_a), .B(decoder_1_b),
    .C(decoder_1_c), .D(decoder_1_d), .E(decoder_1_e), .F(decoder_1_f), .G(decoder_1_g));
  assign Vermelho = divisor_1_p9 & {{4{Palpite}}, 4'b1111};  // AND_Gate and_2, 8 bits wide
  assign Azul = divisor_1_p10 & {{4{Palpite}}, 4'b1111};  // AND_Gate and_3, 8 bits wide
  _7_Segment_Display u_7_segment_display_1 (
    .g(decoder_1_g), .f(decoder_1_f), .a(decoder_1_a), .b(decoder_1_b), .e(decoder_1_e), .d(decoder_1_d),
    .c(decoder_1_c));  // open: dp
endmodule

module main_aberto (
  input  Palpite,
  input  [3:0] in_2,
  output [7:0] Vermelho,
  output [7:0] Azul
);

  wire and_1_out, Comparador_out_9, decoder_1_a, decoder_1_b, decoder_1_c, decoder_1_d, decoder_1_e,
       decoder_1_f, decoder_1_g, main_1_led1, main_1_led2, main_1_led3, main_1_led4, Reset;
  wire [3:0] random_1_out;
  wire [7:0] divisor_1_p9, divisor_1_p10;

  Button u_RESET (.out(Reset));
  Random #(.width(4), .trigger("falling")) random_1 (.clk(Reset), .out(random_1_out));  // open: next, clr
  \Diferença_main  main_1 (
    .Alet_4(random_1_out[3]), .Alet_3(random_1_out[2]), .Alet_2(random_1_out[1]), .Alet_1(random_1_out[0]),
    .Bit_4(in_2[3]), .Bit3(in_2[2]), .Bit2(in_2[1]), .Bit1(in_2[0]), .Led4(main_1_led4), .Led3(main_1_led3),
    .Led2(main_1_led2), .Led1(main_1_led1));
  comparador Comparador (
    .in_1(random_1_out[3]), .C8(in_2[3]), .in_3(random_1_out[2]), .C4(in_2[2]), .in_5(random_1_out[1]),
    .C2(in_2[1]), .in_7(random_1_out[0]), .C1(in_2[0]), .out_9(Comparador_out_9));
  // Divisor divisor_1: pin names not known; wires that end beside it: main_1_led4, main_1_led3, main_1_led2, main_1_led1, main_1_led4, main_1_led3, main_1_led2, main_1_led1, divisor_1_p9, divisor_1_p10
  LED led_1 (.in(and_1_out));
  and and_1 (and_1_out, Comparador_out_9, Palpite);
  decoder decoder_1 (
    .P0(in_2[3]), .P1(in_2[2]), .P2(in_2[1]), .P3(in_2[0]), .A(decoder_1_a), .B(decoder_1_b),
    .C(decoder_1_c), .D(decoder_1_d), .E(decoder_1_e), .F(decoder_1_f), .G(decoder_1_g));
  assign Vermelho = divisor_1_p9 & {{4{Palpite}}, 4'b1111};  // AND_Gate and_2, 8 bits wide
  // RGBLed #(.multibit("true")) rgbled_1: pin names not known; wires that end beside it: and_1_out, main_1_led4, main_1_led3, main_1_led2, main_1_led1, Vermelho, Azul
  assign Azul = divisor_1_p10 & {{4{Palpite}}, 4'b1111};  // AND_Gate and_3, 8 bits wide
  _7_Segment_Display u_7_segment_display_1 (
    .g(decoder_1_g), .f(decoder_1_f), .a(decoder_1_a), .b(decoder_1_b), .e(decoder_1_e), .d(decoder_1_d),
    .c(decoder_1_c));  // open: dp
endmodule

module Jogo (
  input  in_1,
  input  [3:0] in_2
);

  wire button_1_out, decoder_1_a, decoder_1_b, decoder_1_c, decoder_1_d, decoder_1_e, decoder_1_f,
       decoder_1_g, main_1_out_6, \separação_decoder_1_out_2 , \separação_decoder_1_out_3 ,
       \separação_decoder_1_out_4 , \separação_decoder_1_out_5 ;
  wire [7:0] main_1_azul, main_1_vermelho;

  main main_1 (
    .Vermelho(main_1_vermelho), .Azul(main_1_azul), .Palpite(in_1), .in_3(in_2), .out_6(main_1_out_6),
    .in_1(button_1_out));
  Button button_1 (.out(button_1_out));
  // RGBLed #(.multibit("true")) rgbled_1: pin names not known; wires that end beside it: main_1_vermelho, main_1_azul
  LED led_1 (.in(main_1_out_6));
  \Separação_decoder  \separação_decoder_1  (
    .in_1(in_2), .out_2(\separação_decoder_1_out_2 ), .out_3(\separação_decoder_1_out_3 ),
    .out_4(\separação_decoder_1_out_4 ), .out_5(\separação_decoder_1_out_5 ));
  decoder decoder_1 (
    .P0(\separação_decoder_1_out_5 ), .P1(\separação_decoder_1_out_4 ), .P2(\separação_decoder_1_out_3 ),
    .P3(\separação_decoder_1_out_2 ), .A(decoder_1_a), .B(decoder_1_b), .C(decoder_1_c), .D(decoder_1_d),
    .E(decoder_1_e), .F(decoder_1_f), .G(decoder_1_g));
  _7_Segment_Display u_7_segment_display_1 (
    .g(decoder_1_g), .f(decoder_1_f), .a(decoder_1_a), .b(decoder_1_b), .e(decoder_1_e), .d(decoder_1_d),
    .c(decoder_1_c));  // open: dp
endmodule

module \Separação_decoder  (
  input  [3:0] in_1,
  output out_2,
  output out_3,
  output out_4,
  output out_5
);


  assign out_2 = in_1[0];
  assign out_3 = in_1[1];
  assign out_4 = in_1[2];
  assign out_5 = in_1[3];
endmodule
