// Logisim project comp+dec.circ as structural Verilog: 4 circuits, main circuit main
module main (
  input  _8,
  input  _4,
  input  _2,
  input  _1
);

  wire circuito_1_p5, circuito_1_p6, circuito_1_p7, circuito_1_p8, circuito_1_p9, circuito_1_p10,
       circuito_1_p11, comparador_1_out_9;

  // circuito circuito_1: pin names not known; wires that end beside it: _8, _4, _2, _1, circuito_1_p5, circuito_1_p6, circuito_1_p7, circuito_1_p8, circuito_1_p9, circuito_1_p10, circuito_1_p11
  LED led_1 (.in(comparador_1_out_9));
  comparador comparador_1 (
    .in_3(_8), .C4(_4), .in_5(_2), .C2(_1), .out_9(comparador_1_out_9));  // open: in_1, C8, in_7, C1
  _7_Segment_Display u_7_segment_display_1 (
    .g(circuito_1_p11), .f(circuito_1_p10), .a(circuito_1_p5), .b(circuito_1_p6), .e(circuito_1_p9),
    .d(circuito_1_p8), .c(circuito_1_p7));  // open: dp
endmodule

module comparador (
  input  in_1,
  input  C8,
  input  in_3,
  input  C4,
  input  in_5,
  input  C2,
  input  in_7,
  input  C1,
  output out_9
);

  wire xnor_1_out, xnor_2_out, xnor_3_out, xnor_4_out;

  xnor xnor_1 (xnor_1_out, in_1, C8);
  xnor xnor_2 (xnor_2_out, in_3, C4);
  xnor xnor_3 (xnor_3_out, in_5, C2);
  xnor xnor_4 (xnor_4_out, in_7, C1);
  and and_1 (out_9, xnor_1_out, xnor_2_out, xnor_3_out, xnor_4_out);
endmodule

module decoder (
  input  P0,
  input  P1,
  input  P2,
  input  P3,
  output A,
  output B,
  output C,
  output D,
  output E,
  output F,
  output G
);

  wire and_1_out, and_2_out, and_3_out, and_4_out, and_5_out, and_6_out, and_7_out, and_8_out, and_9_out,
       and_10_out, and_11_out, and_12_out, and_13_out, and_14_out, and_15_out, and_16_out, and_17_out,
       and_18_out, and_19_out, and_20_out, and_21_out, and_22_out, and_23_out, and_24_out, and_25_out,
       and_26_out, and_27_out, and_28_out, and_29_out, and_30_out, and_31_out, and_32_out, and_33_out,
       and_34_out, and_35_out, not_1_out, not_2_out, not_3_out, not_4_out, not_5_out, not_6_out, not_7_out,
       not_8_out, not_9_out, not_10_out, not_11_out, not_12_out, not_13_out, not_14_out, not_15_out,
       not_16_out, not_17_out, not_18_out, not_19_out, not_20_out, not_21_out, not_22_out, not_23_out,
       not_24_out, not_25_out, not_26_out, not_27_out, not_28_out, not_29_out, not_30_out, not_31_out,
       not_32_out, not_33_out, not_34_out, not_35_out, not_36_out, not_37_out, not_38_out, not_39_out,
       not_40_out, not_41_out, not_42_out, not_43_out, not_44_out;

  not not_1 (not_1_out, P1);
  and and_1 (and_1_out, not_1_out, not_2_out);
  not not_2 (not_2_out, P3);
  not not_3 (not_3_out, P0);
  and and_2 (and_2_out, not_3_out, P2);
  not not_4 (not_4_out, P0);
  and and_3 (and_3_out, not_4_out, P1, P3);
  and and_4 (and_4_out, P1, P2);
  not not_5 (not_5_out, P1);
  and and_5 (and_5_out, P0, not_5_out, not_6_out);
  not not_6 (not_6_out, P2);
  and and_6 (and_6_out, P0, not_7_out);
  not not_7 (not_7_out, P3);
  not not_8 (not_8_out, P0);
  and and_7 (and_7_out, not_8_out, not_9_out);
  not not_9 (not_9_out, P1);
  not not_10 (not_10_out, P0);
  and and_8 (and_8_out, not_10_out, not_11_out, not_12_out);
  not not_11 (not_11_out, P2);
  not not_12 (not_12_out, P3);
  not not_13 (not_13_out, P1);
  and and_9 (and_9_out, not_13_out, not_14_out);
  not not_14 (not_14_out, P3);
  not not_15 (not_15_out, P0);
  and and_10 (and_10_out, not_15_out, P2, P3);
  and and_11 (and_11_out, P0, not_16_out, P3);
  not not_16 (not_16_out, P2);
  not not_17 (not_17_out, P0);
  and and_12 (and_12_out, not_17_out, not_18_out);
  not not_18 (not_18_out, P2);
  not not_19 (not_19_out, P0);
  and and_13 (and_13_out, not_19_out, P3);
  not not_20 (not_20_out, P2);
  and and_14 (and_14_out, not_20_out, P3);
  not not_21 (not_21_out, P0);
  and and_15 (and_15_out, not_21_out, P1);
  and and_16 (and_16_out, P0, not_22_out);
  not not_22 (not_22_out, P1);
  not not_23 (not_23_out, P0);
  not not_24 (not_24_out, P1);
  and and_17 (and_17_out, not_23_out, not_24_out, not_25_out);
  not not_25 (not_25_out, P3);
  not not_26 (not_26_out, P1);
  and and_18 (and_18_out, not_26_out, P2, P3);
  and and_19 (and_19_out, P1, not_27_out, P3);
  not not_27 (not_27_out, P2);
  and and_20 (and_20_out, P1, P2, not_28_out);
  not not_28 (not_28_out, P3);
  and and_21 (and_21_out, P0, not_29_out, not_30_out);
  not not_29 (not_29_out, P2);
  not not_30 (not_30_out, P3);
  not not_31 (not_31_out, P1);
  and and_22 (and_22_out, not_31_out, not_32_out);
  not not_32 (not_32_out, P3);
  and and_23 (and_23_out, P2, not_33_out);
  not not_33 (not_33_out, P3);
  and and_24 (and_24_out, P0, P2);
  and and_25 (and_25_out, P0, P1);
  not not_34 (not_34_out, P2);
  and and_26 (and_26_out, not_34_out, not_35_out);
  not not_35 (not_35_out, P3);
  not not_36 (not_36_out, P0);
  and and_27 (and_27_out, not_36_out, P1, not_37_out);
  not not_37 (not_37_out, P2);
  and and_28 (and_28_out, P1, not_38_out);
  not not_38 (not_38_out, P3);
  and and_29 (and_29_out, P0, not_39_out);
  not not_39 (not_39_out, P1);
  and and_30 (and_30_out, P0, P2);
  not not_40 (not_40_out, P1);
  and and_31 (and_31_out, not_40_out, P2);
  and and_32 (and_32_out, P2, not_41_out);
  not not_41 (not_41_out, P3);
  not not_42 (not_42_out, P0);
  and and_33 (and_33_out, not_42_out, P1, not_43_out);
  not not_43 (not_43_out, P2);
  and and_34 (and_34_out, P0, not_44_out);
  not not_44 (not_44_out, P1);
  and and_35 (and_35_out, P0, P3);
  or or_1 (B, and_7_out, and_8_out, and_9_out, and_10_out, and_11_out);
  or or_2 (C, and_12_out, and_13_out, and_14_out, and_15_out, and_16_out);
  or or_3 (D, and_17_out, and_18_out, and_19_out, and_20_out, and_21_out);
  or or_4 (E, and_22_out, and_23_out, and_24_out, and_25_out);
  or or_5 (F, and_26_out, and_27_out, and_28_out, and_29_out, and_30_out);
  or or_6 (G, and_31_out, and_32_out, and_33_out, and_34_out, and_35_out);
  or or_7 (A, and_1_out, and_2_out, and_3_out, and_4_out, and_5_out, and_6_out);
endmodule

module decoder_display (
  input  in_1,
  input  in_2,
  input  in_3,
  input  in_4
);

  wire circuito_1_p5, circuito_1_p6, circuito_1_p7, circuito_1_p8, circuito_1_p9, circuito_1_p10,
       circuito_1_p11;

  // circuito circuito_1: pin names not known; wires that end beside it: in_1, in_2, in_3, in_4, circuito_1_p5, circuito_1_p6, circuito_1_p7, circuito_1_p8, circuito_1_p9, circuito_1_p10, circuito_1_p11
  _7_Segment_Display u_7_segment_display_1 (
    .g(circuito_1_p11), .f(circuito_1_p10), .a(circuito_1_p5), .b(circuito_1_p6), .e(circuito_1_p9),
    .d(circuito_1_p8), .c(circuito_1_p7));  // open: dp
endmodule
